# Fritzing sketch feather_co2 (saved by Fritzing 0.9.4b)

parts:
  Part1 = Adafruit FeatherWing Proto [part_number="Adafruit #2884"]
  J2 = male pin header, 5 pins [form="♂ (male)"]
  IC1 = IC, DIP package, 10 pins [chip_label=CozIR-A]
  IC2 = IC, SIP package, 6 pins [chip_label=ZS-042]
  IC4 = IC, SIP package, 7 pins [chip_label=BME280]
  IC3 = IC, SIP package, 5 pins [chip_label=SGP30]

nets:
  N1: Part1.H, Part1.N$109, IC2.pin2
  N2: Part1.SCL, Part1.N$79, Part1.N$80, Part1.N$83, Part1.N$114, Part1.N$115, Part1.N$116, Part1.N$117, Part1.N$118, IC2.pin3, IC4.pin4, IC3.pin4
  N3: Part1.SDA, Part1.N$77, Part1.N$78, Part1.N$104, Part1.N$105, Part1.N$121, Part1.N$122, Part1.N$123, IC2.pin4, IC4.pin6, IC3.pin5
  N4: Part1.G, Part1.N$119, Part1.N$120, Part1.N$125, Part1.N$126, IC2.pin6, IC4.pin3
  N5: Part1.GND, Part1.N$48, Part1.N$84, Part1.N$85, IC1.pin1, IC3.pin3
  N6: Part1.3V, Part1.N$43, Part1.N$94, Part1.N$95, Part1.N$124, Part1.N$128, Part1.N$129, Part1.N$132, Part1.N$133, IC1.pin2, IC2.pin5, IC4.pin1, IC3.pin1
  N7: Part1.N$35, J2.pin1, IC1.pin6
  N8: Part1.N$36, IC1.pin5
  N9: Part1.N$37, IC1.pin4
  N10: Part1.N$38, J2.pin2, IC1.pin7
  N11: Part1.N$41, J2.pin3
  N12: Part1.N$42, IC1.pin3
  N13: Part1.N$44, J2.pin4
  N14: Part1.N$47, J2.pin5
  N15: Part1.N$93, IC3.pin2
  N16: Part1.N$103, IC4.pin7
  N17: Part1.N$108, IC2.pin1
  N18: Part1.N$113, IC4.pin5
  N19: Part1.N$130, IC4.pin2

custom parts:
  Adafruit FeatherWing Proto: This is the FeatherWing Proto - a prototyping add-on for all Feather boards. Using our Feather Stacking Headers or Feather Female Headers you can connect a FeatherWing on top or bottom of your Feather board and let the board take flight! This has a duplicate breakout for each pin on a Feather, as well as a bunch of plain grid proto holes. For GND and 3.3V, we give you a strip of connected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
